// Logisim project Noam_FPGA_CPU.circ as structural Verilog: 9 circuits, main circuit main
module main (
  output [11:0] CURRENT_ADDRESS
);

  wire and_1_out, and_2_out, and_3_out, and_14_out, and_15_out, and_16_out, and_23_out, and_24_out,
       and_25_out, and_26_out, and_27_out, Arithmetic_Logic_Unit_1_c_flag, Arithmetic_Logic_Unit_1_z_flag,
       Clock_Generator_inverse_clock, Clock_Generator_main_clock, counter_1_carry, demultiplexer_1_out0,
       demultiplexer_1_out1, demultiplexer_2_out0, demultiplexer_2_out1, demultiplexer_3_out0,
       demultiplexer_3_out1, demultiplexer_4_out0, demultiplexer_4_out1, keyboard_1_avail, Master_Clock_out,
       Memory_Mapped_IO_ascii_write, Memory_Mapped_IO_hex_write, Memory_Mapped_IO_ram_store_out,
       Memory_Mapped_IO_screen_value, Memory_Mapped_IO_screen_x, Memory_Mapped_IO_screen_y, not_1_out,
       not_2_out, or_1_out, or_3_out, or_7_out, or_8_out, Reg_Selector_1_load_a, Reg_Selector_1_load_b,
       Reg_Selector_1_load_c, Reg_Selector_1_load_d, Reg_Selector_1_out_a, Reg_Selector_1_out_b,
       Reg_Selector_1_out_c, Reg_Selector_1_out_d;
  wire [1:0] IR_reg_select;
  wire [2:0] counter_1_q;
  wire [3:0] SP_value_out_2;
  wire [4:0] Button_1_out;
  wire [5:0] rgb_video_1_p3, rgb_video_1_p4;
  wire [6:0] keyboard_1_data, or_2_out;
  wire [6:3] IR_out_to_microcode_rom;
  wire [7:0] A_ccumulator_perma_out, and_4_out, and_5_out, and_6_out, and_7_out, and_8_out, and_9_out,
       and_10_out, and_11_out, and_12_out, and_13_out, Arithmetic_Logic_Unit_1_result, B_perma_out,
       bit_extender_1_out, bit_extender_2_out, bit_extender_3_out, bit_extender_4_out, bit_extender_5_out,
       bit_extender_6_out, bit_extender_7_out, C_perma_out, D_perma_out, Hex_Driver_1_all_out, MAIN_RAM_dout,
       Memory_Mapped_IO_data_out, or_6_out, rgb_video_1_p5, SP_value_out, T_perma_out, undriven_2;
  wire [7:7] Memory_Mapped_IO_ascii_read, Memory_Mapped_IO_ram_load_out, Memory_Mapped_IO_switch_button_read,
       or_2_out_2;
  wire [11:0] and_18_out, and_19_out, and_20_out, and_21_out, and_22_out, CALL_STACK_dout,
       Memory_Mapped_IO_ram_adress_out, or_4_out, or_5_out, PC_value_out, Programmed_Address_Loader_value_out;
  wire [11:8] undriven_3;
  wire [11:11] and_17_out, not_3_out, undriven_4;
  wire [14:12] undriven;
  wire [31:0] ROM_1_data;

  Clock Master_Clock (.out(Master_Clock_out));
  and and_1 (and_1_out, undriven[13], undriven_4[11]);
  and and_2 (and_2_out, undriven[12], undriven_4[11]);
  // Probe on IR_reg_select
  clock_unit Clock_Generator (
    .Switch_14_Clock_Mode(undriven[14]), .Switch_13_Clock_Step(undriven[13]),
    .Switch_15_Main_Mode(undriven_4[11]), .MASTER_CLOCK(Master_Clock_out), .Halt(ROM_1_data[30]),
    .Switch_12(undriven[12]), .UART_Unhalt(keyboard_1_avail), .Main_Clock(Clock_Generator_main_clock),
    .Inverse_Clock(Clock_Generator_inverse_clock));
  Reg_Selector Reg_Selector_1 (
    .LOAD_A_control(ROM_1_data[0]), .Reg_Select(IR_reg_select), .CODED_REG_LOAD_control(ROM_1_data[1]),
    .CODED_REG_OUT_control(ROM_1_data[2]), .Load_A(Reg_Selector_1_load_a), .Out_A(Reg_Selector_1_out_a),
    .Load_B(Reg_Selector_1_load_b), .Out_B(Reg_Selector_1_out_b), .Load_C(Reg_Selector_1_load_c),
    .Out_C(Reg_Selector_1_out_c), .Load_D(Reg_Selector_1_load_d), .Out_D(Reg_Selector_1_out_d));
  or or_1 (or_1_out, counter_1_carry, ROM_1_data[31]);
  and and_3 (and_3_out, or_1_out, Clock_Generator_inverse_clock);
  assign and_4_out = undriven_2 & bit_extender_1_out;  // AND_Gate and_4, 8 bits wide
  assign bit_extender_1_out = {{7{undriven_4[11]}}, undriven_4[11]};  // Bit_Extender bit_extender_1
  Counter #(.max('h7), .width(3)) counter_1 (
    .load(and_3_out), .D(3'b000), .count(Clock_Generator_inverse_clock), .Q(counter_1_q),
    .carry(counter_1_carry), .up(1'b1), .clk(Master_Clock_out), .clr(1'b0));
  assign and_5_out = A_ccumulator_perma_out & bit_extender_2_out;  // AND_Gate and_5, 8 bits wide
  assign bit_extender_2_out = {{7{Reg_Selector_1_out_a}}, Reg_Selector_1_out_a};  // Bit_Extender bit_extender_2
  ROM #(.addrWidth(7), .dataWidth(32)) ROM_1 (.addr({IR_out_to_microcode_rom, counter_1_q}), .data(ROM_1_data));
  assign and_6_out = Arithmetic_Logic_Unit_1_result & bit_extender_3_out;  // AND_Gate and_6, 8 bits wide
  assign bit_extender_3_out = {{7{ROM_1_data[3]}}, ROM_1_data[3]};  // Bit_Extender bit_extender_3
  Register_8_Bit A_ccumulator (
    .OUT_control(1'b0), .LOAD_control(Reg_Selector_1_load_a), .Master_Clock(Master_Clock_out),
    .Value_In({or_2_out_2[7], or_2_out}), .Main_Clock(Clock_Generator_main_clock),
    .Perma_Out(A_ccumulator_perma_out));  // open: Value_Out
  Arithmetic_Logic_Unit Arithmetic_Logic_Unit_1 (
    .Accummulator_In(A_ccumulator_perma_out), .FLAG_LATCH_control(ROM_1_data[8]),
    .FUNCTION_control(ROM_1_data[6:4]), .FUNCTION_LATCH_control(ROM_1_data[7]),
    .Data_In({or_2_out_2[7], or_2_out}), .LOAD_Control(ROM_1_data[9]),
    .Main_Clock(Clock_Generator_main_clock), .Master_Clock(Master_Clock_out),
    .Result(Arithmetic_Logic_Unit_1_result), .Z_flag(Arithmetic_Logic_Unit_1_z_flag),
    .C_Flag(Arithmetic_Logic_Unit_1_c_flag));
  Register_8_Bit B (
    .OUT_control(1'b0), .LOAD_control(Reg_Selector_1_load_b), .Master_Clock(Master_Clock_out),
    .Value_In({or_2_out_2[7], or_2_out}), .Main_Clock(Clock_Generator_main_clock), .Perma_Out(B_perma_out));  // open: Value_Out
  Register_8_Bit C (
    .OUT_control(1'b0), .LOAD_control(Reg_Selector_1_load_c), .Master_Clock(Master_Clock_out),
    .Value_In({or_2_out_2[7], or_2_out}), .Main_Clock(Clock_Generator_main_clock), .Perma_Out(C_perma_out));  // open: Value_Out
  Register_8_Bit D (
    .OUT_control(1'b0), .LOAD_control(Reg_Selector_1_load_d), .Master_Clock(Master_Clock_out),
    .Value_In({or_2_out_2[7], or_2_out}), .Main_Clock(Clock_Generator_main_clock), .Perma_Out(D_perma_out));  // open: Value_Out
  Register_8_Bit T (
    .OUT_control(1'b0), .LOAD_control(ROM_1_data[11]), .Master_Clock(Master_Clock_out),
    .Value_In({or_2_out_2[7], or_2_out}), .Main_Clock(Clock_Generator_main_clock), .Perma_Out(T_perma_out));  // open: Value_Out
  Instruction_Register IR (
    .REG1_OUT_control(ROM_1_data[12]), .REG2_OUT_control(ROM_1_data[13]), .Master_Clock(Master_Clock_out),
    .Main_Clock(Clock_Generator_main_clock), .LOAD_control(ROM_1_data[14]),
    .Value_In({or_2_out_2[7], or_2_out}), .Reg_Select(IR_reg_select),
    .Out_To_Microcode_ROM(IR_out_to_microcode_rom));
  assign bit_extender_4_out = {{7{Reg_Selector_1_out_b}}, Reg_Selector_1_out_b};  // Bit_Extender bit_extender_4
  assign and_7_out = B_perma_out & bit_extender_4_out;  // AND_Gate and_7, 8 bits wide
  assign and_8_out = C_perma_out & bit_extender_5_out;  // AND_Gate and_8, 8 bits wide
  assign bit_extender_5_out = {{7{Reg_Selector_1_out_c}}, Reg_Selector_1_out_c};  // Bit_Extender bit_extender_5
  assign and_9_out = D_perma_out & bit_extender_6_out;  // AND_Gate and_9, 8 bits wide
  assign bit_extender_6_out = {{7{Reg_Selector_1_out_d}}, Reg_Selector_1_out_d};  // Bit_Extender bit_extender_6
  assign and_10_out = T_perma_out & bit_extender_7_out;  // AND_Gate and_10, 8 bits wide
  assign bit_extender_7_out = {{7{ROM_1_data[10]}}, ROM_1_data[10]};  // Bit_Extender bit_extender_7
  assign {or_2_out_2[7], or_2_out} = and_4_out | and_5_out | and_6_out | and_7_out | and_8_out | and_9_out | and_10_out | and_11_out | and_12_out | and_13_out;  // OR_Gate or_2, 8 bits wide
  assign and_11_out = or_6_out & {8{Memory_Mapped_IO_switch_button_read[7]}};  // AND_Gate and_11, 8 bits wide
  assign and_12_out = MAIN_RAM_dout & {8{Memory_Mapped_IO_ram_load_out[7]}};  // AND_Gate and_12, 8 bits wide
  assign and_13_out = {1'b0, keyboard_1_data} & {8{Memory_Mapped_IO_ascii_read[7]}};  // AND_Gate and_13, 8 bits wide
  // Probe on {or_2_out_2[7], or_2_out}
  or or_3 (or_3_out, and_15_out, and_14_out, demultiplexer_1_out0);
  and and_14 (and_14_out, not_1_out, ROM_1_data[17]);
  not not_1 (not_1_out, Arithmetic_Logic_Unit_1_c_flag);
  and and_15 (and_15_out, not_2_out, ROM_1_data[16]);
  not not_2 (not_2_out, Arithmetic_Logic_Unit_1_z_flag);
  Demultiplexer #(.enable("false")) demultiplexer_1 (
    .out0(demultiplexer_1_out0), .out1(demultiplexer_1_out1), .in(ROM_1_data[21]), .sel(ROM_1_data[20]));
  Demultiplexer #(.enable("false")) demultiplexer_2 (
    .out0(demultiplexer_2_out0), .out1(demultiplexer_2_out1), .in(ROM_1_data[22]), .sel(ROM_1_data[20]));
  RAM #(.dataWidth(12)) CALL_STACK (
    .addr(SP_value_out), .we(and_16_out), .oe(1'b1), .clk(Master_Clock_out), .din(or_5_out),
    .dout(CALL_STACK_dout));
  // NoConnect on SP_value_out_2
  and and_16 (and_16_out, ROM_1_data[18], Clock_Generator_main_clock);
  Increment_Decrement_Register_12_Bit PC (
    .Value_In({or_2_out_2[7], or_2_out}), .Main_Clock(Clock_Generator_main_clock),
    .OUT_control(ROM_1_data[15]), .LOAD_HIGH_Control(demultiplexer_3_out0),
    .LOAD_LOW_Control(demultiplexer_4_out0), .Increment(or_3_out), .Decrement(demultiplexer_2_out0),
    .Master_Clock(Master_Clock_out), .Perma_Out(1'b0), .Value_In_Long(or_5_out), .Value_Out(PC_value_out));
  Increment_Decrement_Register_12_Bit SP (
    .Value_In({8{1'b0}}), .Main_Clock(Clock_Generator_main_clock), .OUT_control(1'b1),
    .LOAD_HIGH_Control(1'b0), .LOAD_LOW_Control(1'b0), .Increment(demultiplexer_1_out1),
    .Decrement(demultiplexer_2_out1), .Master_Clock(Master_Clock_out), .Perma_Out(1'b1),
    .Value_In_Long({12{1'b0}}), .Value_Out({SP_value_out_2, SP_value_out}));
  and and_17 (and_17_out[11], Clock_Generator_main_clock, ROM_1_data[19]);
  Demultiplexer #(.enable("false")) demultiplexer_3 (
    .out0(demultiplexer_3_out0), .out1(demultiplexer_3_out1), .in(ROM_1_data[24]), .sel(ROM_1_data[23]));
  Demultiplexer #(.enable("false")) demultiplexer_4 (
    .out0(demultiplexer_4_out0), .out1(demultiplexer_4_out1), .in(ROM_1_data[25]), .sel(ROM_1_data[23]));
  assign or_4_out = and_18_out | and_19_out | and_20_out;  // OR_Gate or_4, 12 bits wide
  assign and_18_out = CALL_STACK_dout & {12{and_17_out[11]}};  // AND_Gate and_18, 12 bits wide
  assign and_19_out = PC_value_out & {12{ROM_1_data[15]}};  // AND_Gate and_19, 12 bits wide
  assign and_20_out = Programmed_Address_Loader_value_out & {12{ROM_1_data[26]}};  // AND_Gate and_20, 12 bits wide
  not not_3 (not_3_out[11], undriven_4[11]);
  assign and_21_out = or_4_out & {12{not_3_out[11]}};  // AND_Gate and_21, 12 bits wide
  assign and_22_out = {undriven_3, undriven_2} & {12{undriven_4[11]}};  // AND_Gate and_22, 12 bits wide
  // Probe on or_5_out
  assign or_5_out = and_21_out | and_22_out;  // OR_Gate or_5, 12 bits wide
  assign or_6_out = undriven_2 | {3'b000, Button_1_out};  // OR_Gate or_6, 8 bits wide
  TTY #(.cols(80), .rows(16)) tty_1 (
    .data(or_2_out), .clk(Master_Clock_out), .we(Memory_Mapped_IO_ascii_write), .clr(and_23_out));
  and and_23 (and_23_out, Memory_Mapped_IO_ascii_write, or_2_out_2[7]);
  // DipSwitch #(.number(16)) Main_Switches: pin names not known; wires that end beside it: 1'b0, 1'b0
  Keyboard keyboard_1 (
    .clk(Master_Clock_out), .re(Memory_Mapped_IO_ascii_read[7]), .clr(1'b0), .avail(keyboard_1_avail),
    .data(keyboard_1_data));
  Increment_Decrement_Register_12_Bit Programmed_Address_Loader (
    .Value_In({or_2_out_2[7], or_2_out}), .Main_Clock(Clock_Generator_main_clock),
    .OUT_control(ROM_1_data[26]), .LOAD_HIGH_Control(demultiplexer_3_out1),
    .LOAD_LOW_Control(demultiplexer_4_out1), .Increment(1'b0), .Decrement(1'b0),
    .Master_Clock(Master_Clock_out), .Perma_Out(1'b0), .Value_In_Long({12{1'b0}}),
    .Value_Out(Programmed_Address_Loader_value_out));
  Hex_Digit_Display Hex_Digit_Display_2 (.value(Hex_Driver_1_all_out[7:4]));  // open: dp
  Hex_Digit_Display Hex_Digit_Display_3 (.value(Hex_Driver_1_all_out[3:0]));  // open: dp
  Hex_Driver Hex_Driver_1 (
    .Data_In({or_2_out_2[7], or_2_out}), .LOAD_control(Memory_Mapped_IO_hex_write),
    .Master_clock(Master_Clock_out), .All_Out(Hex_Driver_1_all_out));
  and and_24 (and_24_out, Clock_Generator_main_clock, ROM_1_data[27]);
  and and_25 (and_25_out, not_3_out[11], and_24_out);
  Button Button_1 (.out(Button_1_out[0]));
  or or_7 (or_7_out, and_1_out, and_25_out);
  Register #(.width(12)) register_1 (
    .D(or_5_out), .en(or_7_out), .clk(Master_Clock_out), .Q(CURRENT_ADDRESS), .clr(1'b0));
  Button Button_2 (.out(Button_1_out[1]));
  Button Button_3 (.out(Button_1_out[2]));
  Button Button_5 (.out(Button_1_out[4]));
  Button Button_4 (.out(Button_1_out[3]));
  and and_26 (and_26_out, Clock_Generator_main_clock, ROM_1_data[28]);
  // RGB_Video #(.height(64), .reset("Synchronous"), .scale(8), .width(64)) rgb_video_1: pin names not known; wires that end beside it: Master_Clock_out, Master_Clock_out, rgb_video_1_p3, rgb_video_1_p4, rgb_video_1_p5
  or or_8 (or_8_out, and_2_out, and_27_out);
  and and_27 (and_27_out, ROM_1_data[29], Clock_Generator_main_clock);
  Register #(.width(6)) register_2 (
    .D(or_2_out[5:0]), .en(Memory_Mapped_IO_screen_x), .clk(Master_Clock_out), .Q(rgb_video_1_p3), .clr(1'b0));
  // NoConnect on {or_2_out_2[7], or_2_out[6]}
  Register #(.width(6)) register_3 (
    .D(or_2_out[5:0]), .en(Memory_Mapped_IO_screen_y), .clk(Master_Clock_out), .Q(rgb_video_1_p4), .clr(1'b0));
  // NoConnect on {or_2_out_2[7], or_2_out[6]}
  Register register_4 (
    .D({or_2_out_2[7], or_2_out}), .en(Memory_Mapped_IO_screen_value), .clk(Master_Clock_out),
    .Q(rgb_video_1_p5), .clr(1'b0));
  I_O_Driver Memory_Mapped_IO (
    .RAM_ADDRESS_IN(CURRENT_ADDRESS), .RAM_DATA_IN({or_2_out_2[7], or_2_out}), .RAM_LOAD_control(and_26_out),
    .RAM_STORE_control(or_8_out), .HEX_WRITE(Memory_Mapped_IO_hex_write),
    .ASCII_WRITE(Memory_Mapped_IO_ascii_write), .SCREEN_X(Memory_Mapped_IO_screen_x),
    .SCREEN_Y(Memory_Mapped_IO_screen_y), .SCREEN_VALUE(Memory_Mapped_IO_screen_value),
    .SWITCH_BUTTON_READ(Memory_Mapped_IO_switch_button_read[7]), .ASCII_Read(Memory_Mapped_IO_ascii_read[7]),
    .RAM_ADRESS_OUT(Memory_Mapped_IO_ram_adress_out), .DATA_OUT(Memory_Mapped_IO_data_out),
    .RAM_LOAD_OUT(Memory_Mapped_IO_ram_load_out[7]), .RAM_STORE_OUT(Memory_Mapped_IO_ram_store_out));
  RAM #(.addrWidth(12), .\type ("nonvolatile")) MAIN_RAM (
    .addr(Memory_Mapped_IO_ram_adress_out), .we(Memory_Mapped_IO_ram_store_out), .oe(1'b1),
    .clk(Master_Clock_out), .din(Memory_Mapped_IO_data_out), .dout(MAIN_RAM_dout));

  // Notes on the sheet:
  //   contents of ROM_1 (hex, n*v repeats v):
  //   8008000 10004000 1804 80202402 80200000 0 0 0 8008000 10004000 12b4 8020210a 4*0 8008000 10004000
  //   12c4 8020210a 4*0 8008000 10004000 1284 8020210a 4*0 8008000 10004000 1294 8020210a 4*0 8008000
  //   10004000 12a4 8020210a 4*0 8008000 10004000 12d4 8020200a 4*0 8008000 10004000 12e4 8020200a 4*0
  //   8008000 10004000 10200800 9808400 12800000 c000000 90200001 0 8008000 10004000 10200800 9808400
  //   12800000 c000000 a0200004 0 8008000 10004000 20000 20000 80200000 0 0 0 8008000 10004000 10000 10000
  //   80200000 0 0 0 8008000 10004000 10200800 8008000 12000000 81000400 0 0 8008000 10004000 10200800
  //   8208000 300000 12048000 81000400 0 8008000 10004000 3080000 80500000 4*0 8008000 10004000 c0200000
  //   Load_A
  //   Coded_Reg_Load
  //   Loaded_Reg_Out
  //   ALU_Out
  //   ALU_Function
  //   ALU_Function
  //   ALU_Function
  //   ALU_Function_Latch
  //   ALU_Flag_Latch
  //   ALU_Load
  //   T_Out
  //   T_Load
  //   IR_Reg1_Out
  //   IR_Reg2_Out
  //   IR_Load
  //   PC_Out
  //   PC_Increment_If_Not_Zero
  //   PC_Increment_If_Not_Carry
  //   Stack_In
  //   STACK_Out
  //   Increment_Decrement_Select
  //   Increment
  //   Decrement
  //   High_Low_Load_Select
  //   Load_High
  //   Load_Low
  //   Programmed_Address_Out
  //   MAR_Load
  //   RAM_Load
  //   RAM_Store
  //   Halt
  //   Microcode_Reset
endmodule

module clock_unit (
  input  Switch_14_Clock_Mode,
  input  Switch_13_Clock_Step,
  input  Switch_15_Main_Mode,
  input  MASTER_CLOCK,
  input  Halt,
  input  Switch_12,
  input  UART_Unhalt,
  output Main_Clock,
  output Inverse_Clock
);

  wire and_1_out, and_2_out, and_3_out, and_4_out, and_5_out, and_6_out, and_7_out, and_8_out, d_ff_1_q,
       j_k_ff_1_q, j_k_ff_1_qn, not_1_out, not_2_out, not_3_out, or_1_out, s_r_ff_1_qn;

  and and_1 (and_1_out, Switch_15_Main_Mode, Main_Clock);
  and and_2 (and_2_out, Switch_14_Clock_Mode, s_r_ff_1_qn);
  and and_3 (and_3_out, Switch_13_Clock_Step, s_r_ff_1_qn);
  not not_1 (not_1_out, and_1_out);
  D_Flip_Flop d_ff_1 (.D(Switch_12), .clk(MASTER_CLOCK), .Q(d_ff_1_q), .preset(1'b0), .reset(1'b0));  // open: Qn
  and and_4 (and_4_out, and_2_out, not_1_out);
  and and_5 (and_5_out, and_3_out, not_1_out);
  not not_2 (not_2_out, d_ff_1_q);
  and and_6 (and_6_out, not_1_out, s_r_ff_1_qn);
  and and_7 (and_7_out, Switch_12, not_2_out);
  J_K_Flip_Flop j_k_ff_1 (
    .J(and_6_out), .K(and_6_out), .clk(MASTER_CLOCK), .Q(j_k_ff_1_q), .Qn(j_k_ff_1_qn), .preset(1'b0),
    .reset(1'b0));
  and and_8 (and_8_out, Halt, Inverse_Clock);
  or or_1 (or_1_out, and_7_out, UART_Unhalt);
  S_R_Flip_Flop s_r_ff_1 (
    .S(and_8_out), .R(or_1_out), .clk(MASTER_CLOCK), .reset(1'b0), .Qn(s_r_ff_1_qn), .preset(1'b0));  // open: Q
  not not_3 (not_3_out, and_5_out);
  Multiplexer #(.enable("false")) multiplexer_1 (.in0(j_k_ff_1_q), .in1(and_5_out), .out(Main_Clock), .sel(and_4_out));
  Multiplexer #(.enable("false")) multiplexer_2 (
    .in0(j_k_ff_1_qn), .in1(not_3_out), .out(Inverse_Clock), .sel(and_4_out));
endmodule

module Register_8_Bit (
  input  OUT_control,
  input  LOAD_control,
  input  Master_Clock,
  input  [7:0] Value_In,
  input  Main_Clock,
  output [7:0] Value_Out,
  output [7:0] Perma_Out
);

  wire and_1_out, and_2_out;

  and and_1 (and_1_out, LOAD_control, Main_Clock);
  Register register_1 (.D(Value_In), .en(and_1_out), .clk(Master_Clock), .Q(Perma_Out), .clr(1'b0));
  and and_2 (and_2_out, OUT_control, Main_Clock);
  assign Value_Out = and_2_out ? Perma_Out : 8'bz;  // Controlled_Buffer controlled_buffer_1
endmodule

module Instruction_Register (
  input  REG1_OUT_control,
  input  REG2_OUT_control,
  input  Master_Clock,
  input  Main_Clock,
  input  LOAD_control,
  input  [7:0] Value_In,
  output [1:0] Reg_Select,
  output [3:0] Out_To_Microcode_ROM
);

  wire [1:0] and_3_out, and_4_out;
  wire [1:1] and_1_out, and_2_out;
  wire [3:0] Register_8_Bit_1_perma_out;

  and and_1 (and_1_out[1], Main_Clock, REG1_OUT_control);
  and and_2 (and_2_out[1], Main_Clock, REG2_OUT_control);
  Register_8_Bit Register_8_Bit_1 (
    .OUT_control(1'b1), .LOAD_control(LOAD_control), .Master_Clock(Master_Clock), .Value_In(Value_In),
    .Main_Clock(Main_Clock), .Perma_Out({Out_To_Microcode_ROM, Register_8_Bit_1_perma_out}));  // open: Value_Out
  assign and_3_out = {2{and_2_out[1]}} & Register_8_Bit_1_perma_out[1:0];  // AND_Gate and_3, 2 bits wide
  assign Reg_Select = and_3_out | and_4_out;  // OR_Gate or_1, 2 bits wide
  assign and_4_out = Register_8_Bit_1_perma_out[3:2] & {2{and_1_out[1]}};  // AND_Gate and_4, 2 bits wide
endmodule

module Reg_Selector (
  input  LOAD_A_control,
  input  [1:0] Reg_Select,
  input  CODED_REG_LOAD_control,
  input  CODED_REG_OUT_control,
  output Load_A,
  output Out_A,
  output Load_B,
  output Out_B,
  output Load_C,
  output Out_C,
  output Load_D,
  output Out_D
);

  wire demultiplexer_1_out0;

  Demultiplexer #(.enable("false"), .select(2)) demultiplexer_1 (
    .out0(demultiplexer_1_out0), .out1(Load_B), .out2(Load_C), .out3(Load_D), .in(CODED_REG_LOAD_control),
    .sel(Reg_Select));
  Demultiplexer #(.enable("false"), .select(2)) demultiplexer_2 (
    .out0(Out_A), .out1(Out_B), .out2(Out_C), .out3(Out_D), .in(CODED_REG_OUT_control), .sel(Reg_Select));
  or or_1 (Load_A, demultiplexer_1_out0, LOAD_A_control);
endmodule

module Increment_Decrement_Register_12_Bit (
  input  [7:0] Value_In,
  input  Main_Clock,
  input  OUT_control,
  input  LOAD_HIGH_Control,
  input  LOAD_LOW_Control,
  input  Increment,
  input  Decrement,
  input  Master_Clock,
  input  Perma_Out,
  input  [11:0] Value_In_Long,
  output [11:0] Value_Out
);

  wire and_1_out, and_2_out, and_3_out, and_5_out, and_6_out, and_7_out, counter_1_carry, or_1_out, or_3_out;
  wire [3:0] or_4_out;
  wire [7:0] or_2_out;
  wire [11:0] and_4_out, bit_extender_1_out, counter_1_q;
  wire [11:11] or_5_out;

  and and_1 (and_1_out, LOAD_LOW_Control, LOAD_HIGH_Control);
  and and_2 (and_2_out, LOAD_HIGH_Control, Main_Clock);
  and and_3 (and_3_out, Main_Clock, LOAD_LOW_Control);
  or or_1 (or_1_out, Increment, Decrement);
  assign bit_extender_1_out = {{11{and_1_out}}, and_1_out};  // Bit_Extender bit_extender_1
  assign and_4_out = bit_extender_1_out & Value_In_Long;  // AND_Gate and_4, 12 bits wide
  and and_5 (and_5_out, Main_Clock, or_1_out);
  assign or_2_out = Value_In | and_4_out[7:0];  // OR_Gate or_2, 8 bits wide
  Counter counter_1 (
    .load(and_3_out), .D(or_2_out), .count(and_5_out), .Q(counter_1_q[7:0]), .carry(counter_1_carry),
    .up(Increment), .clk(Master_Clock), .clr(1'b0));
  or or_3 (or_3_out, Increment, Decrement);
  // NoConnect on Value_In[4]
  // NoConnect on Value_In[5]
  // NoConnect on Value_In[6]
  // NoConnect on Value_In[7]
  and and_6 (and_6_out, or_3_out, Main_Clock, counter_1_carry);
  assign or_4_out = Value_In[3:0] | and_4_out[11:8];  // OR_Gate or_4, 4 bits wide
  Counter #(.max('hf), .width(4)) counter_2 (
    .load(and_2_out), .D(or_4_out), .count(and_6_out), .Q(counter_1_q[11:8]), .up(Increment),
    .clk(Master_Clock), .clr(1'b0));  // open: carry
  and and_7 (and_7_out, Main_Clock, OUT_control);
  or or_5 (or_5_out[11], Perma_Out, and_7_out);
  assign Value_Out = {12{or_5_out[11]}} & counter_1_q;  // AND_Gate and_8, 12 bits wide
endmodule

module I_O_Driver (
  input  [11:0] RAM_ADDRESS_IN,
  input  [7:0] RAM_DATA_IN,
  input  RAM_LOAD_control,
  input  RAM_STORE_control,
  output HEX_WRITE,
  output ASCII_WRITE,
  output SCREEN_X,
  output SCREEN_Y,
  output SCREEN_VALUE,
  output SWITCH_BUTTON_READ,
  output ASCII_Read,
  output [11:0] RAM_ADRESS_OUT,
  output [7:0] DATA_OUT,
  output RAM_LOAD_OUT,
  output RAM_STORE_OUT
);

  wire and_2_out, and_3_out, and_5_out, and_6_out, and_8_out, and_9_out, and_11_out, and_12_out, and_14_out,
       and_15_out, and_17_out, and_18_out, comparator_1_eq, comparator_2_eq, comparator_3_eq,
       comparator_4_eq, comparator_5_eq, comparator_6_eq, comparator_7_eq, not_1_out, not_2_out, not_3_out,
       not_4_out, not_5_out, not_6_out, not_7_out;

  Comparator #(.mode("unsigned"), .width(12)) comparator_1 (
    .a(RAM_ADDRESS_IN), .b({12{1'b1}}), .eq(comparator_1_eq));  // open: gt, lt
  not not_1 (not_1_out, comparator_1_eq);
  and and_1 (HEX_WRITE, comparator_1_eq, RAM_STORE_control);
  and and_2 (and_2_out, not_1_out, RAM_STORE_control);
  and and_3 (and_3_out, not_1_out, RAM_LOAD_control);
  and and_4 (SWITCH_BUTTON_READ, comparator_2_eq, and_3_out);
  Comparator #(.mode("unsigned"), .width(12)) comparator_2 (
    .a(RAM_ADDRESS_IN), .b(12'hffe), .eq(comparator_2_eq));  // open: gt, lt
  not not_2 (not_2_out, comparator_2_eq);
  and and_5 (and_5_out, not_2_out, and_3_out);
  and and_6 (and_6_out, not_2_out, and_2_out);
  and and_7 (ASCII_WRITE, comparator_3_eq, and_6_out);
  Comparator #(.mode("unsigned"), .width(12)) comparator_3 (
    .a(RAM_ADDRESS_IN), .b(12'hffd), .eq(comparator_3_eq));  // open: gt, lt
  not not_3 (not_3_out, comparator_3_eq);
  and and_8 (and_8_out, and_5_out, not_3_out);
  and and_9 (and_9_out, and_6_out, not_3_out);
  and and_10 (ASCII_Read, comparator_4_eq, and_8_out);
  Comparator #(.mode("unsigned"), .width(12)) comparator_4 (
    .a(RAM_ADDRESS_IN), .b(12'hffc), .eq(comparator_4_eq));  // open: gt, lt
  not not_4 (not_4_out, comparator_4_eq);
  and and_11 (and_11_out, not_4_out, and_8_out);
  and and_12 (and_12_out, not_4_out, and_9_out);
  and and_13 (SCREEN_X, comparator_5_eq, and_12_out);
  Comparator #(.mode("unsigned"), .width(12)) comparator_5 (
    .a(RAM_ADDRESS_IN), .b(12'hffb), .eq(comparator_5_eq));  // open: gt, lt
  not not_5 (not_5_out, comparator_5_eq);
  and and_14 (and_14_out, and_11_out, not_5_out);
  and and_15 (and_15_out, and_12_out, not_5_out);
  and and_16 (SCREEN_Y, comparator_6_eq, and_15_out);
  Comparator #(.mode("unsigned"), .width(12)) comparator_6 (
    .a(RAM_ADDRESS_IN), .b(12'hffa), .eq(comparator_6_eq));  // open: gt, lt
  not not_6 (not_6_out, comparator_6_eq);
  and and_17 (and_17_out, and_14_out, not_6_out);
  and and_18 (and_18_out, and_15_out, not_6_out);
  and and_19 (SCREEN_VALUE, comparator_7_eq, and_18_out);
  Comparator #(.mode("unsigned"), .width(12)) comparator_7 (
    .a(RAM_ADDRESS_IN), .b(12'hff9), .eq(comparator_7_eq));  // open: gt, lt
  not not_7 (not_7_out, comparator_7_eq);
  and and_20 (RAM_LOAD_OUT, and_17_out, not_7_out);
  and and_21 (RAM_STORE_OUT, and_18_out, not_7_out);

  assign DATA_OUT = RAM_DATA_IN;
  assign RAM_ADRESS_OUT = RAM_ADDRESS_IN;
endmodule

module Hex_Driver (
  input  [7:0] Data_In,
  input  LOAD_control,
  input  Master_clock,
  output [7:0] All_Out
);

  Register register_1 (.D(Data_In), .en(LOAD_control), .clk(Master_clock), .Q(All_Out), .clr(1'b0));
endmodule

module Arithmetic_Logic_Unit (
  input  [7:0] Accummulator_In,
  input  FLAG_LATCH_control,
  input  [2:0] FUNCTION_control,
  input  FUNCTION_LATCH_control,
  input  [7:0] Data_In,
  input  LOAD_Control,
  input  Main_Clock,
  input  Master_Clock,
  output [7:0] Result,
  output Z_flag,
  output C_Flag
);

  wire adder_1_cout, and_1_out, and_3_out, and_4_out, and_5_out, and_6_out, comparator_1_eq, comparator_2_eq,
       nor_1_out, or_2_out, subtractor_1_bout;
  wire [2:0] register_2_q;
  wire [7:0] adder_1_out, and_2_out, or_1_out, register_1_q, shifter_1_out, shifter_2_out, subtractor_1_out,
       xor_1_out;

  Register register_1 (.D(Data_In), .en(and_1_out), .clk(Master_Clock), .Q(register_1_q), .clr(1'b0));
  and and_1 (and_1_out, LOAD_Control, Main_Clock);
  assign and_2_out = Accummulator_In & register_1_q;  // AND_Gate and_2, 8 bits wide
  assign or_1_out = Accummulator_In | register_1_q;  // OR_Gate or_1, 8 bits wide
  assign xor_1_out = Accummulator_In ^ register_1_q;  // XOR_Gate xor_1, 8 bits wide
  Adder adder_1 (.a(Accummulator_In), .b(register_1_q), .out(adder_1_out), .cin(1'b0), .cout(adder_1_cout));
  Subtractor subtractor_1 (
    .a(Accummulator_In), .b(register_1_q), .out(subtractor_1_out), .bin(1'b0), .bout(subtractor_1_bout));
  Shifter #(.shift("lr")) shifter_1 (.in(register_1_q), .\dist (3'b001), .out(shifter_1_out));
  Shifter shifter_2 (.in(register_1_q), .\dist (3'b001), .out(shifter_2_out));
  Comparator #(.width(3)) comparator_1 (.a(3'b100), .b(register_2_q), .eq(comparator_1_eq));  // open: gt, lt
  and and_3 (and_3_out, comparator_1_eq, subtractor_1_bout);
  Register #(.width(3)) register_2 (
    .D(FUNCTION_control), .en(and_4_out), .clk(Master_Clock), .Q(register_2_q), .clr(1'b0));
  and and_4 (and_4_out, Main_Clock, FUNCTION_LATCH_control);
  Comparator #(.width(3)) comparator_2 (.a(3'b011), .b(register_2_q), .eq(comparator_2_eq));  // open: gt, lt
  and and_5 (and_5_out, adder_1_cout, comparator_2_eq);
  or or_2 (or_2_out, and_5_out, and_3_out);
  Multiplexer #(.enable("false"), .select(3), .width(8)) multiplexer_1 (
    .in0(and_2_out), .in1(or_1_out), .in2(xor_1_out), .in3(adder_1_out), .in4(subtractor_1_out),
    .in5(shifter_1_out), .in6(shifter_2_out), .in7({8{1'b0}}), .out(Result), .sel(register_2_q));
  nor nor_1 (nor_1_out, Result[7], Result[6], Result[5], Result[4], Result[3], Result[2], Result[1], Result[0]);
  and and_6 (and_6_out, FLAG_LATCH_control, Main_Clock);
  Register #(.width(1)) register_3 (.D(nor_1_out), .en(and_6_out), .clk(Master_Clock), .Q(Z_flag), .clr(1'b0));
  Register #(.width(1)) register_4 (.D(or_2_out), .en(and_6_out), .clk(Master_Clock), .Q(C_Flag), .clr(1'b0));
endmodule
